# Fritzing sketch roboto-1-breadboard-v1 (saved by Fritzing 0.9.3b)
breadboards: 1

parts:
  WeMos_D1_Mini1 = WeMos D1 Mini
  IC1 = ULN2003A [package="DIP16 [THT]"]
  IC2 = ULN2003A [package="DIP16 [THT]"]
  MOTOR1 = 28BYJ-48 Stepper Motor
  MOTOR2 = 28BYJ-48 Stepper Motor

nets:
  N1: WeMos_D1_Mini1.5V, IC1.COM_-_Common, IC2.COM_-_Common, MOTOR1.RED
  N2: WeMos_D1_Mini1.D0, IC1.In_1
  N3: WeMos_D1_Mini1.D1, IC2.In_1
  N4: WeMos_D1_Mini1.D2, IC2.In_2
  N5: WeMos_D1_Mini1.D3, IC2.In_3
  N6: WeMos_D1_Mini1.D4, IC2.In_4
  N7: WeMos_D1_Mini1.D5, IC1.In_2
  N8: WeMos_D1_Mini1.D6, IC1.In_3
  N9: WeMos_D1_Mini1.D7, IC1.In_4
  N10: WeMos_D1_Mini1.G, IC1.0V, IC2.0V, MOTOR2.RED
  N11: IC1.Out_4, MOTOR1.ORANGE
  N12: IC1.Out_3, MOTOR1.YELLOW
  N13: IC1.Out_2, MOTOR1.PINK
  N14: IC1.Out_1, MOTOR1.BLUE
  N15: IC2.Out_4, MOTOR2.ORANGE
  N16: IC2.Out_3, MOTOR2.YELLOW
  N17: IC2.Out_2, MOTOR2.PINK
  N18: IC2.Out_1, MOTOR2.BLUE

custom parts:
  28BYJ-48 Stepper Motor: 28BYJ-48 gear-reduction stepper motor (small)
